# Fritzing sketch Катапульта (saved by Fritzing 0.9.3b)
breadboards: 1

parts:
  Часть1 = Arduino Nano (Rev3.0)
  R1 = Resistor [tolerance=±5% resistance=220 package=THT]
  R2 = Resistor [tolerance=±5% resistance=220 package=THT]
  VCC1 = Battery
  S1 = Pushbutton [package="[THT]"]
  S2 = Pushbutton [package="[THT]"]
  J1 = Basic Servo
  J2 = Basic Servo

nets:
  N1: Часть1.D2, J1.pulse
  N2: Часть1.D3, S1.Pin_1, S1.Pin_2
  N3: Часть1.D4, J2.pulse
  N4: Часть1.D5, S2.Pin_1
  GND: R1.Pin_1, R2.Pin_1, VCC1.-, J1.gnd, J2.gnd
  VCC: VCC1.+, S1.Pin_3, S1.Pin_4, S2.Pin_4, J1.vcc, J2.vcc

notes:
  Сервопривод постоянного движения
  Сервопривод смещения шкива
  Кнопка нажимается автоматически при зарядке катапульты
  Кнопка запуска и зарядки катапульты
